# Fritzing sketch i2c_shifter (saved by Fritzing 0.7.4b)
breadboards: 1

parts:
  T2 = Basic FET N-Channel [package="TO220 [THT]"]
  Rp2 = Resistor [tolerance=±5% resistance=1k package=THT]
  T3 = Basic FET N-Channel [package="TO220 [THT]"]
  T4 = Basic FET N-Channel [package="TO220 [THT]"]
  Rp1 = Resistor [tolerance=±5% resistance=1k package=THT]
  Rp4 = Resistor [tolerance=±5% resistance=1k package=THT]
  Rp3 = Resistor [tolerance=±5% resistance=1k package=THT]
  SDA2 = male pin header, 1 pin [form="♂ (male)"]
  SCL2 = male pin header, 1 pin [form="♂ (male)"]
  SCL1 = male pin header, 1 pin [form="♂ (male)"]
  SDA1 = male pin header, 1 pin [form="♂ (male)"]
  5V = male pin header, 1 pin [form="♂ (male)"]
  3V3 = male pin header, 1 pin [form="♂ (male)"]
  T1 = Basic FET N-Channel [package="TO220 [THT]"]

nets:
  N1: T2.gate, Rp2.Pin_1, Rp1.Pin_1, 3V3.pin1, T1.gate
  N2: T2.drain, T4.drain
  N3: T2.source, Rp2.Pin_0, SCL1.pin1
  N4: T3.gate, T4.gate, Rp4.Pin_0, Rp3.Pin_0, 5V.pin1
  N5: T3.drain, T1.drain
  N6: T3.source, Rp3.Pin_1, SDA2.pin1
  N7: T4.source, Rp4.Pin_1, SCL2.pin1
  N8: Rp1.Pin_0, SDA1.pin1, T1.source

notes:
  VDD1 (3V3)
  SDA1
  SCL1
  VDD2 (5V)
  SCL2
  SDA2
  i2c bi-shifter
  binerry.de
